// Logisim project harward_arc terminal.circ as structural Verilog: 5 circuits, main circuit main
module main (
);

  wire addr_fe_bit_7, and_1_out, and_2_out, and_3_out, and_4_out, and_5_out, and_6_out, and_7_out,
       button_1_out, cdm_8_mark5_1_data_inst, Cl, code, comparator_1_eq, comparator_2_eq, comparator_3_eq,
       comparator_4_eq, comparator_5_eq, comparator_6_eq, data, end_message, mem,
       message_box_1_terminal_clean, message_box_1_terminal_clock, not_1_out, or_1_out,
       player_field_1_dicplay_clean, player_field_1_display_clock, player_field_2_dicplay_clean,
       player_field_2_display_clock, rd_wr;
  wire [2:0] ID_current_memory;
  wire [3:0] write_cell_1_high, write_cell_1_low, write_cell_2_high, write_cell_2_low;
  wire [3:3] keyboard_1_avail;
  wire [6:0] keyboard_1_data, message_box_1_ascii_code_out, player_field_1_ascii_code,
       player_field_2_ascii_code, register_2_q;
  wire [7:0] addr, addr_8_15, cdm_8_mark5_1_data_out, cdm_8_mark5_1_ps, cdm_8_mark5_1_r0, cdm_8_mark5_1_r1,
       cdm_8_mark5_1_r2, cdm_8_mark5_1_r3, cdm_8_mark5_1_sp, controlled_buffer_2_out,
       controlled_buffer_3_out, data_8_bit, register_1_q, register_3_q, undriven, undriven_2;
  wire [7:3] register_4_q;
  wire [15:0] cdm_8_mark5_1_pc;

  // Probe on cdm_8_mark5_1_r0
  // Probe on cdm_8_mark5_1_r1
  // Probe on cdm_8_mark5_1_r3
  // Probe on cdm_8_mark5_1_r2
  Clock clock_1 (.out(Cl));
  // Probe on cdm_8_mark5_1_sp
  // Probe on cdm_8_mark5_1_ps
  // Probe on cdm_8_mark5_1_pc
  CdM_8_mark5 cdm_8_mark5_1 (
    .clock(Cl), .addr({addr_8_15, addr}), .mem_read(rd_wr), .mem_cycle(mem),
    .data_inst(cdm_8_mark5_1_data_inst), .data_out(cdm_8_mark5_1_data_out),
    .data_in(controlled_buffer_2_out), .r0(cdm_8_mark5_1_r0), .r1(cdm_8_mark5_1_r1), .r2(cdm_8_mark5_1_r2),
    .r3(cdm_8_mark5_1_r3), .PC(cdm_8_mark5_1_pc), .SP(cdm_8_mark5_1_sp), .PS(cdm_8_mark5_1_ps));  // open: IAck, IRQ, vec, halted
  Comparator comparator_1 (.a(8'hfe), .b(addr), .eq(comparator_1_eq));  // open: gt, lt
  // Probe on cdm_8_mark5_1_data_out
  Comparator comparator_2 (.a(8'h7), .b(addr), .eq(comparator_2_eq));  // open: gt, lt
  assign data_8_bit = not_1_out ? cdm_8_mark5_1_data_out : 8'bz;  // Controlled_Buffer controlled_buffer_1
  not not_1 (not_1_out, rd_wr);
  assign controlled_buffer_2_out = rd_wr ? data_8_bit : 8'bz;  // Controlled_Buffer controlled_buffer_2
  Comparator comparator_3 (.a(addr_8_15), .b({8{1'b0}}), .eq(comparator_3_eq));  // open: gt, lt
  and and_1 (and_1_out, ~rd_wr, data, comparator_2_eq);  // AND_Gate
  Decoder #(.disabled(0)) decoder_1 (.out0(code), .out1(data), .sel(cdm_8_mark5_1_data_inst), .en(mem));
  and and_2 (and_2_out, comparator_3_eq, data, comparator_1_eq);
  Register register_1 (.D(undriven), .en(and_1_out), .Q(register_1_q), .clk(Cl));  // open: clr
  Comparator comparator_4 (.a(8'h8), .b(addr), .eq(comparator_4_eq));  // open: gt, lt
  // Probe on {addr_8_15, addr}
  Register register_2 (.D(data_8_bit), .en(and_2_out), .Q({addr_fe_bit_7, register_2_q}), .clk(Cl));  // open: clr
  and and_3 (and_3_out, rd_wr, data, comparator_4_eq);
  assign controlled_buffer_3_out = and_3_out ? register_3_q : 8'bz;  // Controlled_Buffer controlled_buffer_3
  Register register_3 (.D(undriven_2), .en(and_3_out), .Q(register_3_q), .clk(Cl));  // open: clr
  assign data_8_bit = and_4_out ? {end_message, 3'b000, keyboard_1_avail[3], register_2_q[2:0]} : 8'bz;  // Controlled_Buffer controlled_buffer_4
  and and_4 (and_4_out, rd_wr, data, comparator_1_eq);
  player_field player_field_1 (
    .rd_wr(rd_wr), .data_1_bit(data), .bot_user_adress(8'hfc), .addr(addr), .data_8_bit(data_8_bit),
    .ASCII_code(player_field_1_ascii_code), .display_clock(player_field_1_display_clock),
    .dicplay_clean(player_field_1_dicplay_clean));
  TTY #(.rows(12), .cols(13)) tty_1 (
    .data(player_field_1_ascii_code), .clk(player_field_1_display_clock), .clr(player_field_1_dicplay_clean));  // open: we
  Hex_Digit_Display hex_digit_display_1 (.value(write_cell_1_high));  // open: dp
  and and_5 (and_5_out, ~or_1_out, data);  // AND_Gate
  or or_1 (or_1_out, and_4_out, and_6_out);
  Keyboard keyboard_1 (
    .clk(register_2_q[0]), .re(register_2_q[1]), .clr(register_2_q[2]), .avail(keyboard_1_avail[3]),
    .data(keyboard_1_data));
  Hex_Digit_Display hex_digit_display_2 (.value(write_cell_1_low));  // open: dp
  write_cell write_cell_1 (
    .data_8_bit(data_8_bit), .rd_wr(rd_wr), .data_1_bit(data), .Cl(Cl), .\const (8'hf0), .addr(addr),
    .low(write_cell_1_low), .high(write_cell_1_high));
  // RAM ram_1: pin names not known; wires that end beside it: {addr_8_15, addr}, code, 1'b1, data_8_bit
  // RAM ram_2: pin names not known; wires that end beside it: addr, and_5_out, Cl, rd_wr, data_8_bit
  Comparator comparator_5 (.a(8'hfd), .b(addr), .eq(comparator_5_eq));  // open: gt, lt
  and and_6 (and_6_out, rd_wr, data, comparator_5_eq);
  message_box message_box_1 (
    .clock(Cl), .data_8_bit(data_8_bit), .rd_wr(rd_wr), .data_1_bit(data), .addr(addr),
    .ASCII_code_out(message_box_1_ascii_code_out), .terminal_clock(message_box_1_terminal_clock),
    .terminal_clean(message_box_1_terminal_clean), .end_message(end_message),
    .addr_fe__bit___7(addr_fe_bit_7), .buttom(button_1_out));
  TTY #(.cols(40)) tty_2 (
    .data(message_box_1_ascii_code_out), .clk(message_box_1_terminal_clock),
    .clr(message_box_1_terminal_clean));  // open: we
  Button button_1 (.out(button_1_out));
  Comparator comparator_6 (.a(8'hfb), .b(addr), .eq(comparator_6_eq));  // open: gt, lt
  assign data_8_bit = and_6_out ? {1'b0, keyboard_1_data} : 8'bz;  // Controlled_Buffer controlled_buffer_5
  and and_7 (and_7_out, ~rd_wr, data, comparator_6_eq);  // AND_Gate
  Register register_4 (.D(data_8_bit), .en(and_7_out), .Q({register_4_q, ID_current_memory}), .clk(Cl));  // open: clr
  // Probe on {1'b0, keyboard_1_data}
  player_field player_field_2 (
    .rd_wr(rd_wr), .data_1_bit(data), .bot_user_adress(8'hfa), .addr(addr), .data_8_bit(data_8_bit),
    .ASCII_code(player_field_2_ascii_code), .display_clock(player_field_2_display_clock),
    .dicplay_clean(player_field_2_dicplay_clean));
  TTY #(.rows(12), .cols(13)) tty_3 (
    .data(player_field_2_ascii_code), .clk(player_field_2_display_clock), .clr(player_field_2_dicplay_clean));  // open: we
  Hex_Digit_Display hex_digit_display_3 (.value(write_cell_2_high));  // open: dp
  Hex_Digit_Display hex_digit_display_4 (.value(write_cell_2_low));  // open: dp
  write_cell write_cell_2 (
    .data_8_bit(data_8_bit), .rd_wr(rd_wr), .data_1_bit(data), .Cl(Cl), .\const (8'hf1), .addr(addr),
    .low(write_cell_2_low), .high(write_cell_2_high));

  // Notes on the sheet:
  //   Терминал вывода поля пользователя
  //   терминал общения с пользователем
  //   Терминал вывода поля бота
endmodule

module _8_bit_to_7___high (
  input  [7:0] entrance,
  output [6:0] bus_0
);


  assign bus_0 = entrance[6:0];
endmodule

module message_box (
  input  clock,
  input  [7:0] data_8_bit,
  input  rd_wr,
  input  data_1_bit,
  input  [7:0] addr,
  input  buttom,
  input  addr_fe__bit___7,
  output [6:0] ASCII_code_out,
  output terminal_clock,
  output terminal_clean,
  output end_message
);

  wire and_1_out, and_3_out, and_5_out, cmp, comparator_1_eq, counter_1_carry, not_1_out, or_1_out, or_2_out,
       or_3_out, register_1_q, register_2_q;
  wire [3:0] counter_1_q;
  wire [7:0] counter_2_q, demultiplexer_1_out1, rom_1_data;

  and and_1 (and_1_out, data_1_bit, ~rd_wr);  // AND_Gate
  Demultiplexer #(.width(8), .enable("false")) demultiplexer_1 (
    .out1(demultiplexer_1_out1), .in(addr), .sel(and_1_out));  // open: out0
  Comparator comparator_1 (.a({8{1'b1}}), .b(demultiplexer_1_out1), .eq(comparator_1_eq));  // open: gt, lt
  and and_2 (terminal_clean, ~rd_wr, data_1_bit, comparator_1_eq);  // AND_Gate
  not not_1 (not_1_out, terminal_clean);
  and and_3 (and_3_out, terminal_clean, clock);
  Counter #(.width(4), .max('hf), .trigger("falling")) counter_1 (
    .Q(counter_1_q), .carry(counter_1_carry), .clk(terminal_clock), .clr(terminal_clean));  // open: load, D, count
  Counter #(.trigger("falling")) counter_2 (
    .load(terminal_clean), .D(data_8_bit), .count(not_1_out), .Q(counter_2_q), .clk(or_1_out));  // open: carry, clr
  or or_1 (or_1_out, and_3_out, counter_1_carry);
  or or_2 (or_2_out, register_1_q, cmp);
  Register #(.width(1)) register_1 (.D(or_2_out), .Q(register_1_q), .clk(clock), .clr(terminal_clean));  // open: en
  ROM #(.addrWidth(12)) rom_1 (.addr({counter_2_q, counter_1_q}), .data(rom_1_data), .sel(1'b1));
  and and_4 (terminal_clock, ~register_1_q, clock);  // AND_Gate
  _8_bit_to_7___high u_8_bit_to_7_high_1 (.entrance(rom_1_data), .bus_0(ASCII_code_out));
  Comparator #(.width(7)) comparator_2 (.a(ASCII_code_out), .b({7{1'b0}}), .eq(cmp));  // open: gt, lt
  or or_3 (or_3_out, register_2_q, buttom);
  and and_5 (and_5_out, or_3_out, ~addr_fe__bit___7);  // AND_Gate
  Register #(.width(1)) register_2 (.D(and_5_out), .Q(register_2_q), .clk(clock));  // open: en, clr
  and and_6 (end_message, cmp, register_2_q);

  // Other names for the same wires on the sheet: Cl = clock; cl_input = terminal_clock; cmp_res = terminal_clean

  // Notes on the sheet:
  //   эта часть для загрузки адреса
  //   ___
  //   >
  //   ^
  //   |
  //   Эта часть для увеличения счётчика адреса
  //   4 младших за само сообщение
  //   8 старших за номер сообщения
  //   contents of rom_1 (hex, n*v repeats v):
  //   54 68 69 73 20 67 61 6d 65 20 69 73 20 22 53 65 61 20 42 61 74 74 6c 65 22 21 a 48 61 76 65 20 61 20
  //   67 6f 6f 64 20 74 69 6d 65 21 6*a 43 6c 69 63 6b 20 74 68 65 20 22 52 65 64 20 42 75 74 74 6f 6e 22
  //   20 74 6f 20 63 6f 6e 74 69 6e 75 65 2e 11*0 57 65 6c 6c 2c 20 77 65 20 6e 65 65 64 20 74 6f 20 61 72
  //   72 61 6e 67 65 20 74 68 65 20 73 68 69 70 73 2e a 54 68 65 72 65 20 69 73 20 61 20 6b 65 79 62 6f 61
  //   72 64 20 62 65 6c 6f 77 2e a 45 6e 74 65 72 20 74 68 65 20 63 6f 6f 72 64 69 6e 61 74 65 73 20 6f 66
  //   20 74 68 65 20 73 68 69 70 73 a 49 20 77 69 6c 6c 20 61 73 6b 20 66 6f 72 2e a 46 69 72 73 74 20 61
  //   20 6c 65 74 74 65 72 2c 20 74 68 65 6e 20 61 20 64 69 67 69 74 2e a 46 6f 72 20 65 78 61 6d 70 6c 65
  //   3a 20 41 32 20 6f 72 20 61 32 a a 43 6c 69 63 6b 20 74 68 65 20 22 52 65 64 20 42 75 74 74 6f 6e 22
  //   20 74 6f 20 63 6f 6e 74 69 6e 75 65 2e 6*0 53 68 69 70 73 20 63 61 6e 6e 6f 74 20 62 65 20 6e 65 69
  //   67 68 62 6f 72 73 2e a 59 6f 75 20 77 69 6c 6c 20 68 61 76 65 3a a 31 20 73 68 69 70 20 77 69 74 68
  //   20 61 20 6c 65 6e 67 74 68 20 6f 66 20 34 2e a 32 20 73 68 69 70 73 20 33 20 69 6e 20 6c 65 6e 67 74
  //   68 2e a 33 20 73 68 69 70 73 20 32 20 69 6e 20 6c 65 6e 67 74 68 2e a 34 20 73 68 69 70 73 20 31 20
  //   69 6e 20 6c 65 6e 67 74 68 2e a a 43 6c 69 63 6b 20 74 68 65 20 22 52 65 64 20 42 75 74 74 6f 6e 22
  //   20 74 6f 20 63 6f 6e 74 69 6e 75 65 2e 8*0 45 6e 74 65 72 20 74 68 65 20 66 69 72 73 74 20 63 6f 6f
  //   72 64 69 6e 61 74 65 a 6f 66 20 74 68 65 20 73 68 69 70 20 6f 66 20 6c 65 6e 67 74 68 20 34 6*a 43
  //   6c 69 63 6b 20 74 68 65 20 22 52 65 64 20 42 75 74 74 6f 6e 22 20 74 6f 20 63 6f 6e 74 69 6e 75 65
  //   2e 5*0 45 6e 74 65 72 20 74 68 65 20 73 65 63 6f 6e 64 20 63 6f 6f 72 64 69 6e 61 74 65 a 6f 66 20
  //   74 68 65 20 73 68 69 70 20 6f 66 20 6c 65 6e 67 74 68 20 34 6*a 43 6c 69 63 6b 20 74 68 65 20 22 52
  //   65 64 20 42 75 74 74 6f 6e 22 20 74 6f 20 63 6f 6e 74 69 6e 75 65 2e 4*0 45 6e 74 65 72 20 74 68 65
  //   20 66 69 72 73 74 20 63 6f 6f 72 64 69 6e 61 74 65 a 6f 66 20 74 68 65 20 73 68 69 70 20 6f 66 20 6c
  //   65 6e 67 74 68 20 33 6*a 43 6c 69 63 6b 20 74 68 65 20 22 52 65 64 20 42 75 74 74 6f 6e 22 20 74 6f
  //   20 63 6f 6e 74 69 6e 75 65 2e 5*0 45 6e 74 65 72 20 74 68 65 20 73 65 63 6f 6e 64 20 63 6f 6f 72 64
  //   69 6e 61 74 65 a 6f 66 20 74 68 65 20 73 68 69 70 20 6f 66 20 6c 65 6e 67 74 68 20 33 6*a 43 6c 69
  //   63 6b 20 74 68 65 20 22 52 65 64 20 42 75 74 74 6f 6e 22 20 74 6f 20 63 6f 6e 74 69 6e 75 65 2e 4*0
  //   45 6e 74 65 72 20 74 68 65 20 66 69 72 73 74 20 63 6f 6f 72 64 69 6e 61 74 65 a 6f 66 20 74 68 65 20
  //   73 68 69 70 20 6f 66 20 6c 65 6e 67 74 68 20 32 6*a 43 6c 69 63 6b 20 74 68 65 20 22 52 65 64 20 42
  //   75 74 74 6f 6e 22 20 74 6f 20 63 6f 6e 74 69 6e 75 65 2e 5*0 45 6e 74 65 72 20 74 68 65 20 73 65 63
  //   6f 6e 64 20 63 6f 6f 72 64 69 6e 61 74 65 a 6f 66 20 74 68 65 20 73 68 69 70 20 6f 66 20 6c 65 6e 67
  //   74 68 20 32 6*a 43 6c 69 63 6b 20 74 68 65 20 22 52 65 64 20 42 75 74 74 6f 6e 22 20 74 6f 20 63 6f
  //   6e 74 69 6e 75 65 2e 4*0 45 6e 74 65 72 20 6f 6e 65 20 63 6f 6f 72 64 69 6e 61 74 65 20 66 6f 72 20
  //   61 20 73 68 69 70 20 6f 66 20 6c 65 6e 67 74 68 20 31 6*a 43 6c 69 63 6b 20 74 68 65 20 22 52 65 64
  //   20 42 75 74 74 6f 6e 22 20 74 6f 20 63 6f 6e 74 69 6e 75 65 2e 12*0 54 68 65 20 66 69 65 6c 64 20 69
  //   73 20 62 65 69 6e 67 20 70 72 69 6e 74 65 64 2e a 50 6c 65 61 73 65 20 77 61 69 74 21 a 20 20 20 50
  //   6c 65 61 73 65 20 77 61 69 74 21 a 6*20 50 6c 65 61 73 65 20 77 61 69 74 21 a 9*20 50 6c 65 61 73 65
  //   20 77 61 69 74 21 a 12*20 50 6c 65 61 73 65 20 77 61 69 74 21 a 15*20 50 6c 65 61 73 65 20 77 61 69
  //   74 21 a 18*20 50 6c 65 61 73 65 20 77 61 69 74 21 11*0 59 6f 75 20 68 61 76 65 20 65 6e 74 65 72 65
  //   64 20 61 6e 20 69 6e 63 6f 72 72 65 63 74 20 73 79 6d 62 6f 6c 73 2e a 50 6c 65 61 73 65 20 74 72 79
  //   20 61 67 61 69 6e 2e 6*a 43 6c 69 63 6b 20 74 68 65 20 22 52 65 64 20 42 75 74 74 6f 6e 22 20 74 6f
  //   20 63 6f 6e 74 69 6e 75 65 2e 15*0 59 6f 75 20 68 61 76 65 20 65 6e 74 65 72 65 64 20 63 6f 6f 72 64
  //   69 6e 61 74 65 73 a 6f 66 20 69 6e 63 6f 72 72 65 63 74 20 6c 65 6e 67 74 68 2e a 50 6c 65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
endmodule

module player_field (
  input  rd_wr,
  input  data_1_bit,
  input  [7:0] bot_user_adress,
  input  [7:0] addr,
  input  [7:0] data_8_bit,
  output display_clock,
  output dicplay_clean,
  output [6:0] ASCII_code
);

  wire and_1_out, and_2_out, and_3_out, comparator_1_eq, comparator_2_eq;
  wire [7:0] demultiplexer_1_out1;

  Demultiplexer #(.width(8), .enable("false")) demultiplexer_1 (
    .out1(demultiplexer_1_out1), .in(addr), .sel(and_1_out));  // open: out0
  Comparator comparator_1 (.a(bot_user_adress), .b(demultiplexer_1_out1), .eq(comparator_1_eq));  // open: gt, lt
  and and_1 (and_1_out, data_1_bit, ~rd_wr);  // AND_Gate
  and and_2 (and_2_out, ~rd_wr, data_1_bit, and_3_out);  // AND_Gate
  and and_3 (and_3_out, and_1_out, comparator_1_eq);
  and and_4 (display_clock, 1'b1, and_2_out);
  Multiplexer #(.select(5), .width(7), .enable("false")) multiplexer_1 (
    .in0(7'b1111110), .in1(7'b0100011), .in2(7'b0100001), .in3(7'b1011000), .in4(7'b1101111),
    .in5(7'b0100000), .in6(7'b0110000), .in7(7'b0110001), .in8(7'b0110010), .in9(7'b0110011),
    .in10(7'b0110100), .in11(7'b0110101), .in12(7'b0110110), .in13(7'b0110111), .in14(7'b0111000),
    .in15(7'b0111001), .in16(7'b1000001), .in17(7'b1000010), .in18(7'b1000011), .in19(7'b1000100),
    .in20(7'b1000101), .in21(7'b1000110), .in22(7'b1000111), .in23(7'b1001000), .in24(7'b1001001),
    .in25(7'b1001010), .in26(7'b0100000), .in27(7'b0001101), .in28(7'b0100000), .in29(7'b0100000),
    .in30(7'b0100000), .in31({7{1'b0}}), .out(ASCII_code), .sel(data_8_bit[4:0]));
  Comparator comparator_2 (.a(8'h1f), .b(data_8_bit), .eq(comparator_2_eq));  // open: gt, lt
  and and_5 (dicplay_clean, display_clock, comparator_2_eq);
  TTY #(.rows(12), .cols(14)) tty_1 (.data(ASCII_code), .clk(display_clock), .clr(dicplay_clean));  // open: we

  // Notes on the sheet:
  //   для очистки дисплея 31
  //   0 - ничего (~)
  //   2 - занято (!)
  //   5 - пробел
  //   1 - корабль (#)
  //   3 - подбитый корабль (X)
  //   4 - выстрел в ничего (* или +)
  //   6 - 15 = figures
  //   16 - 25 = letters
  //   27 - '\n' (Enter)
endmodule

module write_cell (
  input  [7:0] data_8_bit,
  input  rd_wr,
  input  data_1_bit,
  input  Cl,
  input  [7:0] \const ,
  input  [7:0] addr,
  output [3:0] low,
  output [3:0] high
);

  wire and_1_out, comparator_1_eq;
  wire [7:0] register_1_q;

  Comparator comparator_1 (.a(\const ), .b(addr), .eq(comparator_1_eq));  // open: gt, lt
  and and_1 (and_1_out, ~rd_wr, data_1_bit, comparator_1_eq);  // AND_Gate
  Register register_1 (.D(data_8_bit), .en(and_1_out), .Q(register_1_q), .clk(Cl));  // open: clr
  ROM rom_1 (.addr(register_1_q), .data({high, low}));  // open: sel

  // Notes on the sheet:
  //   contents of rom_1 (hex, n*v repeats v):
  //   0 1 2 3 4 5 6 7 8 9 10 11 12 13 14 15 16 17 18 19 20 21 22 23 24 25 26 27 28 29 30 31 32 33 34 35 36
  //   37 38 39 40 41 42 43 44 45 46 47 48 49 50 51 52 53 54 55 56 57 58 59 60 61 62 63 64 65 66 67 68 69
  //   70 71 72 73 74 75 76 77 78 79 80 81 82 83 84 85 86 87 88 89 90 91 92 93 94 95 96 97 98 99
endmodule
